// Logisim project hw3-3.circ as structural Verilog: 3 circuits, main circuit Black Box Test
module Black_Box_Test (
  input  b3,
  input  b2,
  input  b1,
  input  b0,
  input  a3,
  input  a2,
  input  a1,
  input  a0,
  input  d0,
  input  d1,
  output c_out,
  output s3,
  output s2,
  output s1,
  output s0
);

  ALU alu_1 (
    .d0(d0), .d1(d1), .c_out(c_out), .b3(b3), .b2(b2), .b1(b1), .b0(b0), .a3(a3), .a2(a2), .a1(a1), .a0(a0),
    .s3(s3), .s2(s2), .s1(s1), .s0(s0));

  // Notes on the sheet:
  //   ALU Control d1 d0
  //   00 = add 
  //   01 = inc 
  //   10 = sub 
  //   11 = dec 
  //   Black Box Testing of 4-bit ALU
endmodule

// 4-bit ALU
module ALU (
  input  b3,
  input  b2,
  input  b1,
  input  b0,
  input  a3,
  input  a2,
  input  a1,
  input  a0,
  input  d0,
  input  d1,
  output c_out,
  output s3,
  output s2,
  output s1,
  output s0
);

  wire full_adder_2_cout, full_adder_3_cout, full_adder_4_cout, undriven, undriven_2, undriven_3, undriven_4,
       undriven_5;

  Full_Adder full_adder_1 (.cin(full_adder_2_cout), .x(a3), .y(undriven_2), .Sum(s3), .cout(c_out));
  Full_Adder full_adder_2 (.cin(full_adder_3_cout), .x(a2), .y(undriven_3), .Sum(s2), .cout(full_adder_2_cout));
  Full_Adder full_adder_3 (.cin(full_adder_4_cout), .x(a1), .y(undriven_4), .Sum(s1), .cout(full_adder_3_cout));
  Full_Adder full_adder_4 (.cin(undriven), .x(a0), .y(undriven_5), .Sum(s0), .cout(full_adder_4_cout));

  // Notes on the sheet:
  //   c_in
  //   x3
  //   x2
  //   x1
  //   x0
endmodule

// FA
module Full_Adder (
  input  cin,
  input  x,
  input  y,
  output Sum,
  output cout
);

  wire and_1_out, and_2_out, xor_1_out;

  and and_1 (and_1_out, x, y);
  xor xor_1 (xor_1_out, x, y);
  and and_2 (and_2_out, cin, xor_1_out);
  xor xor_2 (Sum, cin, xor_1_out);
  or or_1 (cout, and_2_out, and_1_out);

  // Notes on the sheet:
  //   Full Adder
endmodule
